// Logisim project ALU-Control.circ as structural Verilog: 1 circuit, main circuit ALU-Control
module ALU_Control (
  input  [1:0] ALUOp,
  input  [5:0] Function_Field,
  output [5:0] ALU_Control_Out,
  output Shift
);

  wire and_1_out, and_2_out, and_3_out, and_4_out, and_5_out, and_6_out, and_7_out, and_8_out, and_9_out,
       and_10_out, and_11_out;

  and and_1 (and_1_out, ALUOp[1], ~ALUOp[0], Function_Field[5], ~Function_Field[4], ~Function_Field[3], ~Function_Field[2], ~Function_Field[1], ~Function_Field[0]);  // AND_Gate
  and and_2 (and_2_out, ALUOp[1], ~ALUOp[0], Function_Field[5], ~Function_Field[4], ~Function_Field[3], Function_Field[2], ~Function_Field[1], ~Function_Field[0]);  // AND_Gate
  and and_3 (and_3_out, ALUOp[1], ~ALUOp[0], Function_Field[5], ~Function_Field[4], ~Function_Field[3], Function_Field[2], Function_Field[1], ~Function_Field[0]);  // AND_Gate
  and and_4 (and_4_out, ALUOp[1], ~ALUOp[0], Function_Field[5], ~Function_Field[4], Function_Field[3], ~Function_Field[2], Function_Field[1], ~Function_Field[0]);  // AND_Gate
  and and_5 (and_5_out, ALUOp[1], ~ALUOp[0], ~Function_Field[5], ~Function_Field[4], ~Function_Field[3], ~Function_Field[2], Function_Field[1], ~Function_Field[0]);  // AND_Gate
  and and_6 (and_6_out, ~ALUOp[1], ~ALUOp[0]);  // AND_Gate
  and and_7 (and_7_out, ALUOp[1], ~ALUOp[0], ~Function_Field[5], Function_Field[4], Function_Field[3], Function_Field[2], Function_Field[1], Function_Field[0]);  // AND_Gate
  and and_8 (and_8_out, ALUOp[1], ~ALUOp[0], ~Function_Field[5], ~Function_Field[4], ~Function_Field[3], ~Function_Field[2], ~Function_Field[1], ~Function_Field[0]);  // AND_Gate
  and and_9 (and_9_out, ALUOp[1], ~ALUOp[0], Function_Field[5], ~Function_Field[4], Function_Field[3], ~Function_Field[2], Function_Field[1], ~Function_Field[0]);  // AND_Gate
  and and_10 (and_10_out, ALUOp[1], ~ALUOp[0], Function_Field[5], ~Function_Field[4], ~Function_Field[3], Function_Field[2], ~Function_Field[1], Function_Field[0]);  // AND_Gate
  and and_11 (and_11_out, ALUOp[1], ~ALUOp[0], Function_Field[5], ~Function_Field[4], ~Function_Field[3], Function_Field[2], Function_Field[1], ~Function_Field[0]);  // AND_Gate
  and and_12 (ALU_Control_Out[3], ALUOp[1], ~ALUOp[0], ~Function_Field[5], ~Function_Field[4], ~Function_Field[3], ~Function_Field[2], Function_Field[1]);  // AND_Gate
  or or_1 (ALU_Control_Out[0], and_1_out, and_2_out, and_3_out, and_4_out, and_5_out, and_6_out);
  or or_2 (ALU_Control_Out[1], and_7_out, and_2_out, and_8_out, and_9_out);
  or or_3 (ALU_Control_Out[2], and_10_out, and_11_out, and_8_out, and_9_out);
  or or_4 (Shift, ALU_Control_Out[3], and_8_out);

  assign ALU_Control_Out[5:4] = 2'b00;
endmodule
