// Logisim project ALU_Mult_Shift.circ as structural Verilog: 1 circuit, main circuit main
module main (
  input  Cin,
  input  [5:0] Operation_Code,
  input  [31:0] A,
  input  [31:0] B,
  output Cout,
  output OVF,
  output [31:0] C,
  output Zero
);

  wire nor_1_out, not_1_out;
  wire [31:0] alu_32_bit_1_c, multiplier_8_bit_1_result, shift_left_1_output,
       shift_right_logic_or_arithmetic_1_output;

  nor nor_1 (nor_1_out, Operation_Code[0], Operation_Code[1], Operation_Code[2], Operation_Code[3], Operation_Code[4], Operation_Code[5]);
  ALU_32_bit alu_32_bit_1 (
    .OpCode(Operation_Code), .Invert_B_Signal(nor_1_out), .A(A), .B(B), .Cin(Cin), .C(alu_32_bit_1_c),
    .Cout(Cout), .OVF(OVF));
  Shift_Left shift_left_1 (.Input(B), .Shift_Amount(A[4:0]), .Output(shift_left_1_output));
  Shift_Right_Logic_OR_Arithmetic shift_right_logic_or_arithmetic_1 (
    .Input(B), .Shift_Amount(A[4:0]), .Output(shift_right_logic_or_arithmetic_1_output),
    .Arithmetic(not_1_out));
  not not_1 (not_1_out, Operation_Code[0]);
  Multiplier_8_Bit multiplier_8_bit_1 (.Result(multiplier_8_bit_1_result), .A(A), .B(B));
  Multiplexer #(.select(4), .width(32), .disabled(0), .enable("false")) multiplexer_1 (
    .in0(alu_32_bit_1_c), .in1(alu_32_bit_1_c), .in2(multiplier_8_bit_1_result), .in3(alu_32_bit_1_c),
    .in4(alu_32_bit_1_c), .in5(alu_32_bit_1_c), .in6(shift_left_1_output), .in7(alu_32_bit_1_c),
    .in8(shift_right_logic_or_arithmetic_1_output), .in9(shift_right_logic_or_arithmetic_1_output), .out(C),
    .sel(Operation_Code[3:0]));  // open: in10, in11, in12, in13, in14, in15
  nor nor_2 (Zero, C[0], C[1], C[2], C[3], C[4], C[5], C[6], C[7], C[8], C[9], C[10], C[11], C[12], C[13], C[14], C[15], C[16], C[17], C[19], C[20], C[21], C[22], C[23], C[24], C[25], C[26], C[27], C[28], C[29], C[30], C[31], C[18]);

  // Notes on the sheet:
  //   Shift_Left
  //   Shift_Right_Logical_or_Arithmetic
endmodule
