// Logisim project FA4.circ as structural Verilog: 1 circuit, main circuit 4_bit_full_adder
module _4_bit_full_adder (
  input  [3:0] A,
  input  [3:0] B,
  input  Cin,
  output Cout,
  output [3:0] Out
);

  wire FA1_2_cout, FA1_3_cout, FA1_4_cout;

  _1_bit_full_adder FA1 (.A(A[3]), .B(B[3]), .Cin(FA1_2_cout), .S(Out[3]), .Cout(Cout));
  _1_bit_full_adder FA1_2 (.A(A[2]), .B(B[2]), .Cin(FA1_3_cout), .S(Out[2]), .Cout(FA1_2_cout));
  _1_bit_full_adder FA1_3 (.A(A[1]), .B(B[1]), .Cin(FA1_4_cout), .S(Out[1]), .Cout(FA1_3_cout));
  _1_bit_full_adder FA1_4 (.A(A[0]), .B(B[0]), .Cin(Cin), .S(Out[0]), .Cout(FA1_4_cout));

  // Notes on the sheet:
  //   4-bit ripple carry adder
endmodule
