// Logisim project FA8.circ as structural Verilog: 1 circuit, main circuit main
module main (
  input  [7:0] A,
  input  [7:0] B,
  input  Cin,
  output Cout,
  output [7:0] Out
);

  wire n4_bit_full_adder_2_cout;

  _4_bit_full_adder u_4_bit_full_adder_1 (
    .A(A[7:4]), .Cin(n4_bit_full_adder_2_cout), .Cout(Cout), .Out(Out[7:4]), .B(B[7:4]));
  _4_bit_full_adder u_4_bit_full_adder_2 (
    .A(A[3:0]), .Cin(Cin), .Cout(n4_bit_full_adder_2_cout), .Out(Out[3:0]), .B(B[3:0]));
endmodule
