// Logisim project Full_Adder_32_bit.circ as structural Verilog: 1 circuit, main circuit main
module main (
  input  [31:0] A,
  input  Cin,
  input  [31:0] B,
  output [31:0] Sum,
  output Cout
);

  wire main_1_carry_out, main_2_carry_out, main_3_carry_out, main_4_carry_out, main_5_carry_out,
       main_6_carry_out, main_7_carry_out, main_8_carry_out, main_9_carry_out, main_10_carry_out,
       main_11_carry_out, main_12_carry_out, main_13_carry_out, main_14_carry_out, main_15_carry_out,
       main_16_carry_out, main_17_carry_out, main_18_carry_out, main_19_carry_out, main_20_carry_out,
       main_21_carry_out, main_22_carry_out, main_23_carry_out, main_24_carry_out, main_25_carry_out,
       main_26_carry_out, main_27_carry_out, main_28_carry_out, main_29_carry_out, main_30_carry_out,
       main_31_carry_out;

  one_bit_adder_main main_1 (.A(A[0]), .B(B[0]), .Carry(Cin), .Sum(Sum[0]), .Carry_Out(main_1_carry_out));
  one_bit_adder_main main_2 (.A(A[1]), .B(B[1]), .Carry(main_1_carry_out), .Sum(Sum[1]), .Carry_Out(main_2_carry_out));
  one_bit_adder_main main_3 (.A(A[2]), .B(B[2]), .Carry(main_2_carry_out), .Sum(Sum[2]), .Carry_Out(main_3_carry_out));
  one_bit_adder_main main_4 (.A(A[3]), .B(B[3]), .Carry(main_3_carry_out), .Sum(Sum[3]), .Carry_Out(main_4_carry_out));
  one_bit_adder_main main_5 (.A(A[4]), .B(B[4]), .Carry(main_4_carry_out), .Sum(Sum[4]), .Carry_Out(main_5_carry_out));
  one_bit_adder_main main_6 (.A(A[6]), .B(B[6]), .Carry(main_7_carry_out), .Sum(Sum[6]), .Carry_Out(main_6_carry_out));
  one_bit_adder_main main_7 (.A(A[5]), .B(B[5]), .Carry(main_5_carry_out), .Sum(Sum[5]), .Carry_Out(main_7_carry_out));
  one_bit_adder_main main_8 (.A(A[7]), .B(B[7]), .Carry(main_6_carry_out), .Sum(Sum[7]), .Carry_Out(main_8_carry_out));
  one_bit_adder_main main_9 (.A(A[8]), .B(B[8]), .Carry(main_8_carry_out), .Sum(Sum[8]), .Carry_Out(main_9_carry_out));
  one_bit_adder_main main_10 (
    .A(A[9]), .B(B[9]), .Carry(main_9_carry_out), .Sum(Sum[9]), .Carry_Out(main_10_carry_out));
  one_bit_adder_main main_11 (
    .A(A[10]), .B(B[10]), .Carry(main_10_carry_out), .Sum(Sum[10]), .Carry_Out(main_11_carry_out));
  one_bit_adder_main main_12 (
    .A(A[11]), .B(B[11]), .Carry(main_11_carry_out), .Sum(Sum[11]), .Carry_Out(main_12_carry_out));
  one_bit_adder_main main_13 (
    .A(A[12]), .B(B[12]), .Carry(main_12_carry_out), .Sum(Sum[12]), .Carry_Out(main_13_carry_out));
  one_bit_adder_main main_14 (
    .A(A[13]), .B(B[13]), .Carry(main_13_carry_out), .Sum(Sum[13]), .Carry_Out(main_14_carry_out));
  one_bit_adder_main main_15 (
    .A(A[14]), .B(B[14]), .Carry(main_14_carry_out), .Sum(Sum[14]), .Carry_Out(main_15_carry_out));
  one_bit_adder_main main_16 (
    .A(A[15]), .B(B[15]), .Carry(main_15_carry_out), .Sum(Sum[15]), .Carry_Out(main_16_carry_out));
  one_bit_adder_main main_17 (
    .A(A[17]), .B(B[17]), .Carry(main_18_carry_out), .Sum(Sum[17]), .Carry_Out(main_17_carry_out));
  one_bit_adder_main main_18 (
    .A(A[16]), .B(B[16]), .Carry(main_16_carry_out), .Sum(Sum[16]), .Carry_Out(main_18_carry_out));
  one_bit_adder_main main_19 (
    .A(A[18]), .B(B[18]), .Carry(main_17_carry_out), .Sum(Sum[18]), .Carry_Out(main_19_carry_out));
  one_bit_adder_main main_20 (
    .A(A[19]), .B(B[19]), .Carry(main_19_carry_out), .Sum(Sum[19]), .Carry_Out(main_20_carry_out));
  one_bit_adder_main main_21 (
    .A(A[20]), .B(B[20]), .Carry(main_20_carry_out), .Sum(Sum[20]), .Carry_Out(main_21_carry_out));
  one_bit_adder_main main_22 (
    .A(A[21]), .B(B[21]), .Carry(main_21_carry_out), .Sum(Sum[21]), .Carry_Out(main_22_carry_out));
  one_bit_adder_main main_23 (
    .A(A[22]), .B(B[22]), .Carry(main_22_carry_out), .Sum(Sum[22]), .Carry_Out(main_23_carry_out));
  one_bit_adder_main main_24 (
    .A(A[23]), .B(B[23]), .Carry(main_23_carry_out), .Sum(Sum[23]), .Carry_Out(main_24_carry_out));
  one_bit_adder_main main_25 (
    .A(A[24]), .B(B[24]), .Carry(main_24_carry_out), .Sum(Sum[24]), .Carry_Out(main_25_carry_out));
  one_bit_adder_main main_26 (
    .A(A[25]), .B(B[25]), .Carry(main_25_carry_out), .Sum(Sum[25]), .Carry_Out(main_26_carry_out));
  one_bit_adder_main main_27 (
    .A(A[26]), .B(B[26]), .Carry(main_26_carry_out), .Sum(Sum[26]), .Carry_Out(main_27_carry_out));
  one_bit_adder_main main_28 (
    .A(A[27]), .B(B[27]), .Carry(main_27_carry_out), .Sum(Sum[27]), .Carry_Out(main_28_carry_out));
  one_bit_adder_main main_29 (
    .A(A[28]), .B(B[28]), .Carry(main_28_carry_out), .Sum(Sum[28]), .Carry_Out(main_29_carry_out));
  one_bit_adder_main main_30 (
    .A(A[29]), .B(B[29]), .Carry(main_29_carry_out), .Sum(Sum[29]), .Carry_Out(main_30_carry_out));
  one_bit_adder_main main_31 (
    .A(A[30]), .B(B[30]), .Carry(main_30_carry_out), .Sum(Sum[30]), .Carry_Out(main_31_carry_out));
  one_bit_adder_main main_32 (.A(A[31]), .B(B[31]), .Carry(main_31_carry_out), .Sum(Sum[31]), .Carry_Out(Cout));
endmodule
