// Logisim project MIPS_Complete_Processor.circ as structural Verilog: 1 circuit, main circuit main
module main (
);

  wire alu_control_1_shift, and_1_out, and_2_out, and_3_out, Clock_out, main_7_zero, main_control_1_alusrc,
       main_control_1_beq, main_control_1_bge, main_control_1_bne, main_control_1_jump,
       main_control_1_memread, main_control_1_memtoreg, main_control_1_memwrite, main_control_1_regdst,
       main_control_1_regwrite, not_1_out, not_2_out, or_1_out, or_2_out;
  wire [1:0] main_control_1_aluop;
  wire [3:0] main_1_sum, main_1_sum_2, main_1_sum_3, main_1_sum_4, main_1_sum_5, main_1_sum_6, main_1_sum_7,
       main_1_sum_8;
  wire [4:0] multiplexer_1_out;
  wire [5:0] alu_control_1_alu_control_out;
  wire [25:0] rom_1_data;
  wire [27:0] main_3_out_28_bits;
  wire [31:0] main_2_out_32_shifted2, main_4_shift_32bits, main_5_out_32_bits, main_6_sum, main_7_c,
       multiplexer_2_out, multiplexer_3_out, multiplexer_4_out, multiplexer_5_out, ram_1_data, register_1_q,
       registerfile_1_p1, registerfile_1_p7, registerfile_1_p8;
  wire [31:26] rom_1_data_2;

  Clock Clock (.out(Clock_out));
  Full_Adder_32_bit_main main_1 (
    .Cin(1'b0), .A(32'h4), .B(register_1_q),
    .Sum({main_1_sum_8, main_1_sum_7, main_1_sum_6, main_1_sum_5, main_1_sum_4, main_1_sum_3, main_1_sum_2, main_1_sum}));  // open: Cout
  Register #(.width(32)) register_1 (.D(multiplexer_5_out), .en(1'b1), .Q(register_1_q), .clk(Clock_out), .clr(1'b0));
  Shift_right_by_2_32bit_main main_2 (.In_32bit(register_1_q), .Out_32_Shifted2(main_2_out_32_shifted2));
  ShiftLeft26_main main_3 (.In_26_bits(rom_1_data), .Out_28_bits(main_3_out_28_bits));
  ROM #(.addrWidth(24), .dataWidth(32)) rom_1 (
    .addr(main_2_out_32_shifted2[23:0]), .data({rom_1_data_2, rom_1_data}), .sel(1'b1));
  Shift_5_to_32_main main_4 (.Shift_5Bits(rom_1_data[10:6]), .Shift_32Bits(main_4_shift_32bits));
  Main_Control main_control_1 (
    .OpCode_Instruction(rom_1_data_2), .RegDst(main_control_1_regdst), .ALUSrc(main_control_1_alusrc),
    .MemToReg(main_control_1_memtoreg), .RegWrite(main_control_1_regwrite), .MemRead(main_control_1_memread),
    .MemWrite(main_control_1_memwrite), .beq(main_control_1_beq), .bne(main_control_1_bne),
    .bge(main_control_1_bge), .jump(main_control_1_jump), .ALUOp(main_control_1_aluop));
  Multiplexer #(.width(5), .disabled(0), .enable("false")) multiplexer_1 (
    .in0(rom_1_data[20:16]), .in1(rom_1_data[15:11]), .out(multiplexer_1_out), .sel(main_control_1_regdst));
  SignExtend_main main_5 (.In_16_bits(rom_1_data[15:0]), .Out_32_Bits(main_5_out_32_bits));
  // RegisterFile registerfile_1: pin names not known; wires that end beside it: registerfile_1_p1, Clock_out, main_control_1_regwrite, multiplexer_1_out, rom_1_data[25:21], rom_1_data[20:16], registerfile_1_p7, registerfile_1_p8
  Full_Adder_32_bit_main main_6 (
    .Cin(1'b0),
    .A({main_1_sum_8, main_1_sum_7, main_1_sum_6, main_1_sum_5, main_1_sum_4, main_1_sum_3, main_1_sum_2, main_1_sum}),
    .B(main_5_out_32_bits), .Sum(main_6_sum));  // open: Cout
  not not_1 (not_1_out, main_7_zero);
  Multiplexer #(.width(32), .disabled(0), .enable("false")) multiplexer_2 (
    .in0(registerfile_1_p8), .in1(main_5_out_32_bits), .out(multiplexer_2_out), .sel(main_control_1_alusrc));
  Multiplexer #(.width(32), .disabled(0), .enable("false")) multiplexer_3 (
    .in0(registerfile_1_p7), .in1(main_4_shift_32bits), .out(multiplexer_3_out), .sel(alu_control_1_shift));
  ALU_Control alu_control_1 (
    .ALU_Control_Out(alu_control_1_alu_control_out), .ALUOp(main_control_1_aluop),
    .Function_Field(rom_1_data[5:0]), .Shift(alu_control_1_shift));
  and and_1 (and_1_out, main_control_1_bne, not_1_out);
  or or_1 (or_1_out, and_3_out, and_1_out, and_2_out);
  and and_2 (and_2_out, main_control_1_beq, main_7_zero);
  ALU_Mult_Shift_main main_7 (
    .Zero(main_7_zero), .Operation_Code(alu_control_1_alu_control_out), .A(multiplexer_3_out),
    .B(multiplexer_2_out), .Cin(1'b0), .C(main_7_c));  // open: Cout, OVF
  Multiplexer #(.width(32), .disabled(0), .enable("false")) multiplexer_4 (
    .in0({main_1_sum_8, main_1_sum_7, main_1_sum_6, main_1_sum_5, main_1_sum_4, main_1_sum_3, main_1_sum_2, main_1_sum}),
    .in1(main_6_sum), .out(multiplexer_4_out), .sel(or_1_out));
  and and_3 (and_3_out, main_control_1_bge, or_2_out);
  Multiplexer #(.width(32), .disabled(0), .enable("false")) multiplexer_5 (
    .in0(multiplexer_4_out), .in1({main_1_sum_8, main_3_out_28_bits}), .out(multiplexer_5_out),
    .sel(main_control_1_jump));
  not not_2 (not_2_out, main_7_c[31]);
  or or_2 (or_2_out, not_2_out, main_7_zero);
  RAM #(.addrWidth(12), .dataWidth(32), .bus("separate")) ram_1 (
    .addr(main_7_c[11:0]), .din(registerfile_1_p8), .data(ram_1_data), .str(main_control_1_memwrite),
    .sel(1'b1), .clk(Clock_out), .ld(main_control_1_memread), .clr(1'b0));
  Multiplexer #(.width(32), .disabled(0), .enable("false")) multiplexer_6 (
    .in0(main_7_c), .in1(ram_1_data), .out(registerfile_1_p1), .sel(main_control_1_memtoreg));

  // Notes on the sheet:
  //   ShiftAmount
  //   InstructionMem
  //   contents of rom_1 (hex, n*v repeats v):
  //   20050001 20060064 20021000 21400 3cc80008 20470028 28a30000 c3202a 30850002 c33022 2c400000 20420004
  //   3447fff9 2ce60000
  //   bneq
  //   beq
  //   bMUX
  //   jMUX
  //   bge
endmodule
