// Logisim project Main-Control.circ as structural Verilog: 1 circuit, main circuit Main-Control
module Main_Control (
  input  [5:0] OpCode_Instruction,
  output RegDst,
  output ALUSrc,
  output MemToReg,
  output RegWrite,
  output MemRead,
  output MemWrite,
  output beq,
  output bne,
  output bge,
  output jump,
  output [1:0] ALUOp
);

  wire and_2_out, and_3_out;

  and and_1 (ALUOp[1], ~OpCode_Instruction[0], ~OpCode_Instruction[1], ~OpCode_Instruction[2], ~OpCode_Instruction[3], ~OpCode_Instruction[4], ~OpCode_Instruction[5]);  // AND_Gate
  and and_2 (and_2_out, OpCode_Instruction[1], ~OpCode_Instruction[2], OpCode_Instruction[3], ~OpCode_Instruction[4], ~OpCode_Instruction[5]);  // AND_Gate
  and and_3 (and_3_out, ~OpCode_Instruction[0], ~OpCode_Instruction[1], ~OpCode_Instruction[2], OpCode_Instruction[3], ~OpCode_Instruction[4], ~OpCode_Instruction[5]);  // AND_Gate
  and and_4 (MemRead, ~OpCode_Instruction[0], OpCode_Instruction[1], ~OpCode_Instruction[2], OpCode_Instruction[3], ~OpCode_Instruction[4], ~OpCode_Instruction[5]);  // AND_Gate
  and and_5 (MemWrite, OpCode_Instruction[0], OpCode_Instruction[1], ~OpCode_Instruction[2], OpCode_Instruction[3], ~OpCode_Instruction[4], ~OpCode_Instruction[5]);  // AND_Gate
  and and_6 (beq, ~OpCode_Instruction[0], ~OpCode_Instruction[1], OpCode_Instruction[2], OpCode_Instruction[3], ~OpCode_Instruction[4], ~OpCode_Instruction[5]);  // AND_Gate
  and and_7 (bne, OpCode_Instruction[0], ~OpCode_Instruction[1], OpCode_Instruction[2], OpCode_Instruction[3], ~OpCode_Instruction[4], ~OpCode_Instruction[5]);  // AND_Gate
  and and_8 (bge, OpCode_Instruction[0], OpCode_Instruction[1], OpCode_Instruction[2], OpCode_Instruction[3], ~OpCode_Instruction[4], ~OpCode_Instruction[5]);  // AND_Gate
  or or_1 (ALUOp[0], bge, bne, beq);
  and and_9 (jump, ~OpCode_Instruction[0], OpCode_Instruction[1], OpCode_Instruction[2], OpCode_Instruction[3], ~OpCode_Instruction[4], ~OpCode_Instruction[5]);  // AND_Gate
  or or_2 (ALUSrc, and_2_out, and_3_out);
  or or_3 (RegWrite, ALUOp[1], MemRead, and_3_out);

  assign MemToReg = MemRead;
  assign RegDst = ALUOp[1];
endmodule
