// Logisim project Multiplier_8_Bit.circ as structural Verilog: 1 circuit, main circuit Multiplier_8_Bit
module Multiplier_8_Bit (
  input  [31:0] A,
  input  [31:0] B,
  output [31:0] Result
);

  wire [7:0] and_1_out, and_2_out, and_3_out, and_4_out, and_5_out, and_6_out, and_8_out, main_2_cout,
       main_3_cout, main_4_cout, main_5_cout, main_6_cout, main_7_cout;
  wire [7:1] and_7_out;

  assign and_1_out = B[7:0] & {8{A[7]}};  // AND_Gate and_1, 8 bits wide
  FA8_main main_1 (.A(and_1_out), .B(main_2_cout), .Cout(Result[15]), .Out(Result[14:7]), .Cin(1'b0));
  assign and_2_out = B[7:0] & {8{A[6]}};  // AND_Gate and_2, 8 bits wide
  FA8_main main_2 (
    .A(and_2_out), .B(main_3_cout), .Cout(main_2_cout[7]), .Out({main_2_cout[6:0], Result[6]}), .Cin(1'b0));
  assign and_3_out = B[7:0] & {8{A[5]}};  // AND_Gate and_3, 8 bits wide
  assign and_4_out = B[7:0] & {8{A[4]}};  // AND_Gate and_4, 8 bits wide
  FA8_main main_3 (
    .A(and_3_out), .B(main_4_cout), .Cout(main_3_cout[7]), .Out({main_3_cout[6:0], Result[5]}), .Cin(1'b0));
  FA8_main main_4 (
    .A(and_4_out), .B(main_5_cout), .Cout(main_4_cout[7]), .Out({main_4_cout[6:0], Result[4]}), .Cin(1'b0));
  assign and_5_out = B[7:0] & {8{A[3]}};  // AND_Gate and_5, 8 bits wide
  assign and_6_out = B[7:0] & {8{A[2]}};  // AND_Gate and_6, 8 bits wide
  FA8_main main_5 (
    .A(and_5_out), .B(main_6_cout), .Cout(main_5_cout[7]), .Out({main_5_cout[6:0], Result[3]}), .Cin(1'b0));
  FA8_main main_6 (
    .A(and_6_out), .B(main_7_cout), .Cout(main_6_cout[7]), .Out({main_6_cout[6:0], Result[2]}), .Cin(1'b0));
  assign {and_7_out, Result[0]} = B[7:0] & {8{A[0]}};  // AND_Gate and_7, 8 bits wide
  assign and_8_out = B[7:0] & {8{A[1]}};  // AND_Gate and_8, 8 bits wide
  FA8_main main_7 (
    .A(and_8_out), .B({1'b0, and_7_out}), .Cout(main_7_cout[7]), .Out({main_7_cout[6:0], Result[1]}),
    .Cin(1'b0));

  assign A[23:8] = {A[31:24], A[31:24]};
  assign B[31:8] = {A[31:24], A[31:24], A[31:24]};
  assign Result[31:16] = {16{1'b0}};
  // also tied to GND on the sheet: {A[24], A[25], A[26], A[27], A[28], A[29], A[30], A[31]}
endmodule
