// Logisim project ShiftLeft26.circ as structural Verilog: 1 circuit, main circuit main
module main (
  input  [25:0] In_26_bits,
  output [27:0] Out_28_bits
);


  assign Out_28_bits = {In_26_bits, 2'b00};
endmodule
