// Logisim project ShiftLeft32.circ as structural Verilog: 1 circuit, main circuit main
module main (
  input  [31:0] In_32_Bits,
  output [31:0] Out_32_Bits
);


  assign Out_32_Bits = {In_32_Bits[29:0], 2'b00};
endmodule
