// Logisim project Shift_5_to_32.circ as structural Verilog: 1 circuit, main circuit main
module main (
  input  [4:0] Shift_5Bits,
  output [31:0] Shift_32Bits
);


  assign Shift_32Bits = {{27{1'b0}}, Shift_5Bits};
endmodule
