// Logisim project Shift_right_by_2_32bit.circ as structural Verilog: 1 circuit, main circuit main
module main (
  input  [31:0] In_32bit,
  output [31:0] Out_32_Shifted2
);


  assign Out_32_Shifted2 = {2'b00, In_32bit[31:2]};
endmodule
