// Logisim project SignExtend.circ as structural Verilog: 1 circuit, main circuit main
module main (
  input  [15:0] In_16_bits,
  output [31:0] Out_32_Bits
);


  assign Out_32_Bits = {{17{In_16_bits[15]}}, In_16_bits[14:0]};
endmodule
