// Logisim project branch_addr_mul_by_4.circ as structural Verilog: 1 circuit, main circuit main
module main (
  input  [31:0] in,
  output [31:0] out
);


  assign in[0] = in[1];
  assign out[29:0] = in[31:2];
  // also tied to GND on the sheet: in[1]
endmodule
